# Fritzing sketch car (saved by Fritzing 0.9.3b)

parts:
  Part1 = Arduino Nano (Rev3.0)
  Part2 = TE466 [part_number=TE466]
  M1 = DC Motor
  U1 = Mini-360 DC-DC Buck converter [package=THT]
  Part3 = NRF24L01+ Breakout Board
  U2 = LIPO-1000mAh [package=lipo-1000]
  J1 = Basic Servo

nets:
  GND: Part1.GND, Part1.A6, Part2.GND, Part2.SRC_-_GND, Part2.SRC_-_POS, Part2.CS, U1.IN-, U1.IN+, U1.OUT-, Part3.GND, U2.+, U2.-, J1.gnd
  N1: Part1.D4, Part2.INA
  N2: Part1.D5, Part2.INB
  N3: Part1.D6, Part2.PWM
  N4: Part1.D9, Part3.CE
  N5: Part1.D10, Part3.CS
  N6: Part1.D11/MOSI, Part3.MOSI
  N7: Part1.D12/MISO, Part3.MISO
  5V: Part1.5V, Part2.5V, U1.OUT+, Part3.VCC, J1.vcc
  N8: Part1.A7, Part2.EN
  N9: Part1.D13/SCK, Part3.SCK
  N10: Part2.OUTA, M1.pin_1
  N11: Part2.OUTB, M1.pin_2

custom parts:
  TE466: Description: This is essentially a ramped up version of our Ardumoto motor driver shield. For this monster shield we've replaced the L298 H-bridge with a pair of VNH2SP30 full-bridge motor drivers. We've also beefed up the support circuitry so this board is capable of driving a pair of high-current motors! The VIN and motor out are pitched for our 5mm screw terminals (not included), making it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
  Mini-360 DC-DC Buck converter: Mini-360 DC-DC Buck converter. Tiny buck step down voltage converter, input voltage 4.75 to 23V output 1 to 17V adjustable. Available from ebay and the like.
