# Fritzing sketch rc (saved by Fritzing 0.9.3b)

parts:
  Part1 = Arduino Nano (Rev3.0)
  Part2 = NRF24L01+ Breakout Board
  Part3 = Thumb Joystick
  Part4 = Thumb Joystick
  VCC1 = Battery

nets:
  N1: Part1.D9, Part2.CE
  N2: Part1.D10, Part2.CS
  N3: Part1.D11/MOSI, Part2.MOSI
  N4: Part1.D12/MISO, Part2.MISO
  N5: Part1.A1, Part3.VERT
  N6: Part1.A0, Part4.HORZ
  N7: Part1.D13/SCK, Part2.SCK
  GND: Part2.GND, Part3.GND, Part4.GND, VCC1.-
  VCC: Part2.VCC, Part3.VCC, Part4.VCC, VCC1.+
